// Logisim project cpu.circ as structural Verilog: 1 circuit, main circuit main
module main (
  input  [31:0] INSTRUCTION,
  input  CLOCK,
  output [31:0] PROGRAM_COUNTER,
  output [31:0] ra,
  output [31:0] sp,
  output [31:0] t0,
  output [31:0] t1,
  output [31:0] t2,
  output [31:0] s0,
  output [31:0] s1,
  output [31:0] a0
);

  wire branch_comp_1_breq, branch_comp_1_brlt, control_logic_1_brun, control_logic_1_regwen;
  wire [1:0] control_logic_1_wbsel;
  wire [3:0] control_logic_1_alusel;
  wire [4:0] rd, rs1, rs2;
  wire [31:0] adder_1_out, Arithmetic_Logic_Unit_result, DMEM_p2, imm, RegFile_read_data_1, register_1_q, wb;

  Adder #(.width(32)) adder_1 (.a(PROGRAM_COUNTER), .b(32'h4), .out(adder_1_out));  // open: cin, cout
  Register #(.width(32)) PC (.D(adder_1_out), .clk(CLOCK), .Q(PROGRAM_COUNTER));  // open: en, clr
  Register #(.width(32)) register_1 (
    .D(INSTRUCTION), .clk(CLOCK),
    .Q({register_1_q[31:25], rs2, rs1, register_1_q[14:12], rd, register_1_q[6:0]}));  // open: en, clr
  control_logic control_logic_1 (
    .BrUn(control_logic_1_brun), .RegWEn(control_logic_1_regwen), .BrLt(branch_comp_1_brlt),
    .BrEq(branch_comp_1_breq),
    .inst({register_1_q[31:25], rs2, rs1, register_1_q[14:12], rd, register_1_q[6:0]}),
    .ALUSel(control_logic_1_alusel), .WBSel(control_logic_1_wbsel));  // open: BSel, ASel, ImmSel, PCSel, MemRW
  regfile_main RegFile (
    .rs2(rs2), .rd(rd), .Read_Data_1(RegFile_read_data_1), .ra(ra), .sp(sp), .t0(t0), .t1(t1), .t2(t2),
    .s0(s0), .s1(s1), .a0(a0), .rs1(rs1), .Write_Data(wb), .RegWEn(control_logic_1_regwen), .clk(CLOCK));  // open: Read_Data_2
  imm_gen imm_gen_1 (
    .inst({register_1_q[31:25], rs2, rs1, register_1_q[14:12], rd, register_1_q[6:0]}), .imm(imm));  // open: ImmSel
  branch_comp branch_comp_1 (
    .BrEq(branch_comp_1_breq), .BrUn(control_logic_1_brun), .BrLt(branch_comp_1_brlt));  // open: rs1, rs2
  alu Arithmetic_Logic_Unit (
    .ALUSel(control_logic_1_alusel), .Result(Arithmetic_Logic_Unit_result), .A(RegFile_read_data_1), .B(imm));
  // mem_main DMEM: pin names not known; wires that end beside it: CLOCK, DMEM_p2
  Multiplexer #(.select(2), .width(32), .enable("false")) multiplexer_1 (
    .in1(Arithmetic_Logic_Unit_result), .in2(DMEM_p2), .out(wb), .sel(control_logic_1_wbsel));  // open: in0, in3

  // Other names for the same wires on the sheet: clk = CLOCK

  // Notes on the sheet:
  //   Output
  //   IMEM (do **NOT** move this)
  //   Inputs
  //   It is OK to move the PC, RegFile, ALU, MEM, Branch Comp, Imm Gen, and Control Logic to wherever is most convenient for you when constructing your CPU, and to delete this text
  //   Inputs/Outputs for testing. Do **NOT** move these.
endmodule
